# Fritzing sketch bluetooth (saved by Fritzing 0.9.3b)
breadboards: 1

parts:
  Εξάρτημα1 = Arduino Mega 2560 (Rev3)
  Εξάρτημα3 = Bluetooth HC-05 Macho
  R1 = Resistor [tolerance=±5% resistance=2.2k package=THT]
  R2 = Resistor [tolerance=±5% resistance=1k package=THT]

nets:
  N1: Εξάρτημα1.D15/RX3, Εξάρτημα3.TXD
  N2: Εξάρτημα1.D14/TX3, R2.Pin_1
  5V: Εξάρτημα1.5V, Εξάρτημα3.VCC
  GND: Εξάρτημα1.GND, Εξάρτημα3.GND, R1.Pin_1
  N3: Εξάρτημα3.RXD, R1.Pin_0, R2.Pin_0
