# Fritzing sketch full (saved by Fritzing 0.9.3b)
breadboards: 1

parts:
  Εξάρτημα1 = Arduino Mega 2560 (Rev3)
  Εξάρτημα2 = Adafruit Motor/Stepper/Servo Shield [part_number="Adafruit #1438"]
  M1 = DC Motor
  M2 = DC Motor
  M3 = DC Motor
  M4 = DC Motor
  U1 = LIPO-2000mAh [package=lipo-2000]
  S1 = Square Pushbutton
  Εξάρτημα3 = Bluetooth HC-05 Macho
  R1 = Resistor [tolerance=±5% resistance=2.2k package=THT]
  R2 = Resistor [tolerance=±5% resistance=1k package=THT]
  J1 = Generic male header - 6 pins [form="♂ (male)" package=THT]
  Εξάρτημα4 = MQ-7 breakout
  DHT11_1 = DHT11 module
  VCC1 = Battery block 9V  # not connected

nets:
  N1: Εξάρτημα1.A8, J1.S-GND
  N2: Εξάρτημα1.A7, Εξάρτημα4.AO
  N3: Εξάρτημα1.D15/RX3, Εξάρτημα3.TXD
  N4: Εξάρτημα1.D14/TX3, R2.Pin_1
  VCC: Εξάρτημα1.5V, Εξάρτημα3.VCC, J1.VCC, Εξάρτημα4.VCC, DHT11_1.VCC
  N5: Εξάρτημα1.D31, J1.LED
  N6: Εξάρτημα1.D33, DHT11_1.DATA
  GND: Εξάρτημα1.GND, Εξάρτημα3.GND, R1.Pin_1, J1.V0, Εξάρτημα4.GND, DHT11_1.GND
  N7: Εξάρτημα2.M2A, M2.pin_1
  N8: Εξάρτημα2.M2B, M2.pin_2
  N9: Εξάρτημα2.M1B, M1.pin_1
  N10: Εξάρτημα2.M1A, M1.pin_2
  N11: Εξάρτημα2.M3A, M4.pin_2
  N12: Εξάρτημα2.M3B, M4.pin_1
  N13: Εξάρτημα2.M4B, M3.pin_2
  N14: Εξάρτημα2.M4A, M3.pin_1
  N15: Εξάρτημα2.GND, S1.leg0
  N16: Εξάρτημα2.VMOTOR, U1.+
  N17: U1.-, S1.leg1
  N18: Εξάρτημα3.RXD, R1.Pin_0, R2.Pin_0

custom parts:
  Adafruit Motor/Stepper/Servo Shield: The original Adafruit Motorshield kit is one of our most beloved kits, which is why we decided to make something even better. We have upgraded the shield kit to make the bestest, easiest way to drive DC and Stepper motors. This shield will make quick work of your next robotics project! We kept the ability to drive up to 4 DC motors or 2 stepper motors, but added many improvements: Instead of a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
  Generic male header - 6 pins: Generic male header
  MQ-7 breakout: SKU: 101282
  DHT11 module: DHT11 black pcb module
