# Fritzing sketch motors (saved by Fritzing 0.9.3b)

parts:
  Εξάρτημα1 = Arduino Mega 2560 (Rev3)  # not connected
  Εξάρτημα2 = Adafruit Motor/Stepper/Servo Shield [part_number="Adafruit #1438"]
  M1 = DC Motor
  M2 = DC Motor
  M3 = DC Motor
  M4 = DC Motor
  U1 = LIPO-2000mAh [package=lipo-2000]
  S1 = Square Pushbutton
  VCC1 = Battery block 9V  # not connected

nets:
  N1: Εξάρτημα2.M2A, M2.pin_1
  N2: Εξάρτημα2.M2B, M2.pin_2
  N3: Εξάρτημα2.M1B, M1.pin_1
  N4: Εξάρτημα2.M1A, M1.pin_2
  N5: Εξάρτημα2.M3A, M4.pin_2
  N6: Εξάρτημα2.M3B, M4.pin_1
  N7: Εξάρτημα2.M4B, M3.pin_2
  N8: Εξάρτημα2.M4A, M3.pin_1
  N9: Εξάρτημα2.GND, S1.leg0
  N10: Εξάρτημα2.VMOTOR, U1.+
  N11: U1.-, S1.leg1

custom parts:
  Adafruit Motor/Stepper/Servo Shield: The original Adafruit Motorshield kit is one of our most beloved kits, which is why we decided to make something even better. We have upgraded the shield kit to make the bestest, easiest way to drive DC and Stepper motors. This shield will make quick work of your next robotics project! We kept the ability to drive up to 4 DC motors or 2 stepper motors, but added many improvements: Instead of a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
