# Fritzing sketch sensors (saved by Fritzing 0.9.3b)
breadboards: 1

parts:
  Εξάρτημα1 = Arduino Mega 2560 (Rev3)
  J1 = Generic male header - 6 pins [form="♂ (male)" package=THT]
  Εξάρτημα4 = MQ-7 breakout
  DHT11_1 = DHT11 module

nets:
  N1: Εξάρτημα1.A8, J1.S-GND
  N2: Εξάρτημα1.A7, Εξάρτημα4.AO
  VCC: Εξάρτημα1.5V, J1.VCC, Εξάρτημα4.VCC, DHT11_1.VCC
  N3: Εξάρτημα1.D31, J1.LED
  N4: Εξάρτημα1.D33, DHT11_1.DATA
  GND: Εξάρτημα1.GND, J1.V0, Εξάρτημα4.GND, DHT11_1.GND

custom parts:
  Generic male header - 6 pins: Generic male header
  MQ-7 breakout: SKU: 101282
  DHT11 module: DHT11 black pcb module
